# Fritzing sketch sketch (saved by Fritzing 0.9.3b)

parts:
  U1 = ESP8266 NodeMCU LoLin module
  YF-S201_Flow_Meter1 = YF-S201 Water Flow Meter

nets:
  N1: U1.D2, YF-S201_Flow_Meter1.SIG
  VIN: U1.Vin, YF-S201_Flow_Meter1.VCC
  GND: U1.GND, YF-S201_Flow_Meter1.GND

custom parts:
  ESP8266 NodeMCU LoLin module: ESP8266 based NodeMCU
  YF-S201 Water Flow Meter: The YF-S201 Flow Meter. The input voltage is 5V to 24V (DC).
